// Logisim project Exercise3.circ as structural Verilog: 1 circuit, main circuit main
module main (
  input  a,
  input  b,
  output x
);

  wire AND_1_out, AND_2_out, NOT_1_out, NOT_2_out;

  not NOT_1 (NOT_1_out, a);
  not NOT_2 (NOT_2_out, b);
  and AND_1 (AND_1_out, NOT_1_out, b);
  and AND_2 (AND_2_out, a, NOT_2_out);
  or OR (x, AND_1_out, AND_2_out);

  // Notes on the sheet:
  //   Exercise 2
  //                  XOR GATE
  //   x1
  //   x2
endmodule
