// Logisim project Exercise7.circ as structural Verilog: 1 circuit, main circuit main
// IN2
module main (
  input  in_1,
  input  in_2,
  input  in_3,
  input  [7:0] in_4,
  input  in_5,
  input  in_6,
  input  in_7,
  input  [4:0] in_8,
  input  [4:0] in_9,
  input  [4:0] in_10,
  input  [4:0] in_11,
  input  [4:0] in_12,
  output out_13,
  output out_14,
  output out_15,
  output out_16,
  output out_17,
  output out_18,
  output out_19,
  output out_20,
  output out_21,
  output [7:0] out_22
);

  wire nor_1_out, nor_2_out, nor_3_out, nor_4_out, nor_5_out, not_1_out, not_2_out, not_3_out, not_4_out,
       not_5_out;

  assign out_22 = {{7{in_7}}, in_7};  // Bit_Extender bit_extender_1
  not not_1 (not_1_out, in_1);
  not not_2 (not_2_out, in_2);
  not not_3 (not_3_out, in_3);
  not not_4 (not_4_out, in_5);
  not not_5 (not_5_out, in_6);
  nor nor_1 (nor_1_out, not_1_out, in_2);
  nor nor_2 (nor_2_out, not_2_out, in_3);
  nor nor_3 (nor_3_out, not_3_out, in_5);
  nor nor_4 (nor_4_out, not_4_out, in_6);
  nor nor_5 (nor_5_out, not_5_out, in_1);
  DotMatrix #(.inputtype("row"), .matrixrows(5)) dotmatrix_1 (
    .row0(in_8), .row1(in_9), .row2(in_10), .row3(in_11), .row4(in_12));
  and and_1 (out_17, nor_1_out, nor_2_out, nor_3_out, nor_4_out, nor_5_out);

  assign out_13 = in_4[0];
  assign out_14 = in_4[1];
  assign out_15 = in_4[2];
  assign out_16 = in_4[3];
  assign out_18 = in_4[4];
  assign out_19 = in_4[5];
  assign out_20 = in_4[6];
  assign out_21 = in_4[7];

  // Other names for the same wires on the sheet: in = in_7; IN1 = in_1; IN2 = in_2; IN3 = in_3; IN4 = in_5;
  //   IN5 = in_6

  // Notes on the sheet:
  //   CIRCUIT 1
  //   CIRCUIT 2
  //   CIRCUIT 3
  //   circuit 4
endmodule
