// Logisim project GATE.circ as structural Verilog: 1 circuit, main circuit main
module main (
  input  Input1,
  input  Input2,
  input  Input1_2,
  input  Input1_3,
  input  Input2_2,
  input  Input1_4,
  input  Input2_3,
  input  Input1_5,
  input  Input2_4,
  input  Input1_6,
  input  input2_5,
  input  Input1_7,
  input  input2_6,
  output \output ,
  output output_2,
  output output_3,
  output output_4,
  output output_5,
  output output_6,
  output output_7
);

  wire and_1_out, or_2_out;

  not not_1 (output_2, Input1_2);
  and and_1 (and_1_out, Input1, Input2);
  or or_1 (output_5, Input1_5, Input2_4);
  not not_2 (\output , and_1_out);
  not not_3 (output_3, or_2_out);
  or or_2 (or_2_out, Input1_3, Input2_2);
  and and_2 (output_4, Input1_4, Input2_3);
  xor xor_1 (output_6, Input1_6, input2_5);
  xnor xnor_1 (output_7, Input1_7, input2_6);

  // Notes on the sheet:
  //   NOT GATE
  //   NAND GATE
  //   AND GATE
  //   NOR GATE
  //   OR GATE
  //   XOR GATE
  //   XNOR GATE
endmodule
